# Fritzing sketch BLueGateArduino (saved by Fritzing 0.9.4)
breadboards: 1

parts:
  Componente1 = Arduino Uno (Rev3) - ICSP
  Componente2 = Bluetooth HC-05 Macho
  KY-1 = Keyes Relay [package=THT]

nets:
  N1: Componente1.ICSP_MOSI, Componente1.D11_PWM/MOSI, Componente2.RXD
  N2: Componente1.D10_PWM/SS, Componente2.TXD
  N3: Componente1.D13/SCK, KY-1.signal
  5V: Componente1.5V, Componente2.VCC, KY-1.power
  GND: Componente1.GND, Componente2.GND, KY-1.ground

custom parts:
  Keyes Relay: The Keyes 5V relay module is suitable for SCM development, home appliance control. It uses a 5V~12V TIL control signal which can control DC / AC signal.
